// Logisim project tf_arqui.circ as structural Verilog: 6 circuits, main circuit CPU
module CPU (
);

  wire bancoregistrador_1_regwrite, clk, controle_1_memread, controle_1_memwrite, controle_1_muxula,
       controle_1_r0, controle_1_regwrite, idex_1_muxulaex, idex_1_r0ctrlex, MemRead, MemWrite, reset,
       ula_1_zero;
  wire [1:0] controle_1_branchtype, controle_1_muxwrite, MuxWrite;
  wire [2:0] controle_1_ulacontrol, idex_1_ulactrlex;
  wire [7:0] adder_1_out, bancoregistrador_1_saidaa, bancoregistrador_1_saidab, bit_extender_1_out,
       idex_1_immex, idex_1_r0ex, idex_1_regaex, idex_1_regbex, ifid_1_instid, ifid_1_pcid,
       multiplexer_1_out, multiplexer_2_out, PC_q, ram_1_dout, rom_1_data, ula_1_saida, undriven;

  Clock clock_1 (.out(clk));
  Register PC (.D(adder_1_out), .en(1'b1), .clk(clk), .Q(PC_q), .clr(reset));
  Button button_1 (.out(reset));
  Adder adder_1 (.a(8'h1), .b(PC_q), .out(adder_1_out));  // open: cin, cout
  ROM rom_1 (.addr(PC_q), .data(rom_1_data));
  IFID ifid_1 (
    .InstIF(rom_1_data), .PCIF(adder_1_out), .we(1'b1), .reset(reset), .instID(ifid_1_instid),
    .PCID(ifid_1_pcid));
  assign bit_extender_1_out = {{6{ifid_1_instid[3]}}, ifid_1_instid[3:2]};  // Bit_Extender bit_extender_1
  controle controle_1 (
    .in_1(ifid_1_instid[7:4]), .UlaControl(controle_1_ulacontrol), .BranchType(controle_1_branchtype),
    .r0(controle_1_r0), .MemRead(controle_1_memread), .MemWrite(controle_1_memwrite),
    .MuxWrite(controle_1_muxwrite), .MuxUla(controle_1_muxula), .RegWrite(controle_1_regwrite));
  bancoRegistrador bancoregistrador_1 (
    .RegValue(undriven), .RegA(ifid_1_instid[1:0]), .RegB(ifid_1_instid[3:2]), .Reset(reset),
    .RegWrite(bancoregistrador_1_regwrite), .SaidaA(bancoregistrador_1_saidaa),
    .SaidaB(bancoregistrador_1_saidab));
  IDEX idex_1 (
    .BranchTID(controle_1_branchtype), .r0ctrlID(controle_1_r0), .MemReadID(controle_1_memread),
    .MemWriteID(controle_1_memwrite), .MuxWriteID(controle_1_muxwrite), .MuxUlaID(controle_1_muxula),
    .RegWriteID(controle_1_regwrite), .RegAID(bancoregistrador_1_saidaa), .RegBID(bancoregistrador_1_saidab),
    .ImmID(bit_extender_1_out), .pcID(ifid_1_pcid), .UlaCtrlID(controle_1_ulacontrol), .we(1'b1),
    .reset(reset), .r0ctrlEX(idex_1_r0ctrlex), .MuxUlaEX(idex_1_muxulaex), .RegAEX(idex_1_regaex),
    .RegBEX(idex_1_regbex), .R0EX(idex_1_r0ex), .immEX(idex_1_immex), .UlaCtrlEX(idex_1_ulactrlex));  // open: R0ID, RegWriteEX, BranchTEX, MemReadEX, MemWriteEX, MuxWriteEX, pcEX
  Multiplexer #(.width(8)) multiplexer_1 (
    .in0(idex_1_regbex), .in1(idex_1_r0ex), .out(multiplexer_1_out), .sel(idex_1_r0ctrlex));
  Multiplexer #(.width(8)) multiplexer_2 (
    .in0(multiplexer_1_out), .in1(idex_1_immex), .out(multiplexer_2_out), .sel(idex_1_muxulaex));
  Ula ula_1 (
    .A(idex_1_regaex), .B(multiplexer_2_out), .OpULA(idex_1_ulactrlex), .zero(ula_1_zero), .saida(ula_1_saida));
  Multiplexer #(.select(2), .width(8)) multiplexer_3 (.in1(ram_1_dout), .sel(MuxWrite));  // open: in0, in2, in3, out
  RAM #(.trigger("falling")) ram_1 (.we(MemWrite), .oe(MemRead), .clk(clk), .dout(ram_1_dout));  // open: addr, din

  // Notes on the sheet:
  //   contents of rom_1 (hex, n*v repeats v):
  //   ff 0 ff 0 ff
  //   imm
  //   MEMORIA TEMPORARIA
endmodule

module bancoRegistrador (
  input  [7:0] RegValue,
  input  [1:0] RegA,
  input  [1:0] RegB,
  input  Reset,
  output [7:0] SaidaA,
  output [7:0] SaidaB,
  output RegWrite
);

  wire clock_1_out, demultiplexer_1_out0, demultiplexer_1_out1, demultiplexer_1_out2, demultiplexer_1_out3;
  wire [7:0] r0_q, r1_q, r2_q, r3_q;

  Demultiplexer #(.select(2)) demultiplexer_1 (
    .out0(demultiplexer_1_out0), .out1(demultiplexer_1_out1), .out2(demultiplexer_1_out2),
    .out3(demultiplexer_1_out3), .in(RegWrite), .sel(RegA));
  Register r0 (.D(RegValue), .en(demultiplexer_1_out0), .clk(clock_1_out), .Q(r0_q), .clr(Reset));
  Register r1 (.D(RegValue), .en(demultiplexer_1_out1), .clk(clock_1_out), .Q(r1_q), .clr(Reset));
  Clock clock_1 (.out(clock_1_out));
  Register r2 (.D(RegValue), .en(demultiplexer_1_out2), .clk(clock_1_out), .Q(r2_q), .clr(Reset));
  Register r3 (.D(RegValue), .en(demultiplexer_1_out3), .clk(clock_1_out), .Q(r3_q), .clr(Reset));
  Multiplexer #(.select(2), .width(8)) multiplexer_1 (
    .in0(r0_q), .in1(r1_q), .in2(r2_q), .in3(r3_q), .out(SaidaA), .sel(RegA));
  Multiplexer #(.select(2), .width(8)) multiplexer_2 (
    .in0(r0_q), .in1(r1_q), .in2(r2_q), .in3(r3_q), .out(SaidaB), .sel(RegB));
endmodule

module Ula (
  input  [7:0] A,
  input  [7:0] B,
  input  [2:0] OpULA,
  output zero,
  output [7:0] saida
);

  wire [2:0] bit_extender_1_out;
  wire [7:0] adder_1_out, and_1_out, not_1_out, or_1_out, shifter_1_out, shifter_2_out, subtractor_1_out;

  assign not_1_out = ~B;  // NOT_Gate not_1, 8 bits wide
  Bit_Extender #(.out_width(3)) bit_extender_1 (.in(B), .out(bit_extender_1_out));
  Adder adder_1 (.a(A), .b(B), .out(adder_1_out));  // open: cin, cout
  Subtractor subtractor_1 (.a(A), .b(B), .out(subtractor_1_out));  // open: bin, bout
  assign and_1_out = A & B;  // AND_Gate and_1, 8 bits wide
  assign or_1_out = A | B;  // OR_Gate or_1, 8 bits wide
  Shifter shifter_1 (.in(A), .\dist (bit_extender_1_out), .out(shifter_1_out));
  Shifter shifter_2 (.in(A), .\dist (bit_extender_1_out), .out(shifter_2_out));
  Multiplexer #(.select(3), .width(8)) multiplexer_1 (
    .in0(adder_1_out), .in1(subtractor_1_out), .in2(and_1_out), .in3(or_1_out), .in4(not_1_out),
    .in5(shifter_1_out), .in6(shifter_2_out), .out(saida), .sel(OpULA));  // open: in7
  Comparator comparator_1 (.a({8{1'b0}}), .b(saida), .eq(zero));  // open: gt, lt
endmodule

module controle (
  input  [3:0] in_1,
  output [2:0] UlaControl,
  output [1:0] BranchType,
  output r0,
  output MemRead,
  output MemWrite,
  output [1:0] MuxWrite,
  output MuxUla,
  output RegWrite
);

  wire clock_1_out;
  wire [15:12] rom_1_data;

  Register #(.width(4)) ProvaIn (.D(in_1), .en(1'b1), .clk(clock_1_out));  // open: Q, clr
  Clock clock_1 (.out(clock_1_out));
  ROM #(.addrWidth(4), .dataWidth(16)) rom_1 (
    .addr(in_1),
    .data({rom_1_data, RegWrite, MuxUla, MuxWrite, MemWrite, MemRead, r0, BranchType, UlaControl}));
  Register #(.width(16)) ProvaOut (
    .D({rom_1_data, RegWrite, MuxUla, MuxWrite, MemWrite, MemRead, r0, BranchType, UlaControl}), .en(1'b1),
    .clk(clock_1_out));  // open: Q, clr

  // Notes on the sheet:
  //   contents of rom_1 (hex, n*v repeats v):
  //   800 c00 801 802 c02 803 c03 804 805 806 29 10 18 940 80
endmodule

module IFID (
  input  [7:0] InstIF,
  input  [7:0] PCIF,
  input  we,
  input  reset,
  output [7:0] instID,
  output [7:0] PCID
);

  wire clock_1_out;

  Clock clock_1 (.out(clock_1_out));
  Register register_1 (.D(InstIF), .en(we), .clk(clock_1_out), .Q(instID), .clr(reset));
  Register register_2 (.D(PCIF), .en(we), .clk(clock_1_out), .Q(PCID), .clr(reset));
endmodule

module IDEX (
  input  [7:0] pcID,
  input  [7:0] RegAID,
  input  [7:0] RegBID,
  input  [7:0] R0ID,
  input  [7:0] ImmID,
  input  [2:0] UlaCtrlID,
  input  [1:0] BranchTID,
  input  r0ctrlID,
  input  MemReadID,
  input  MemWriteID,
  input  [1:0] MuxWriteID,
  input  MuxUlaID,
  input  RegWriteID,
  input  we,
  input  reset,
  output [7:0] pcEX,
  output [7:0] RegAEX,
  output [7:0] RegBEX,
  output [7:0] R0EX,
  output [7:0] immEX,
  output [2:0] UlaCtrlEX,
  output [1:0] BranchTEX,
  output r0ctrlEX,
  output MemReadEX,
  output MemWriteEX,
  output [1:0] MuxWriteEX,
  output MuxUlaEX,
  output RegWriteEX
);

  wire clock_1_out, undriven, undriven_2;

  Clock clock_1 (.out(clock_1_out));
  Register register_1 (.D(pcID), .en(undriven), .clk(undriven_2), .Q(pcEX), .clr(reset));
  Register register_2 (.D(RegAID), .en(we), .clk(clock_1_out), .Q(RegAEX), .clr(reset));
  Register register_3 (.D(RegBID), .en(we), .clk(clock_1_out), .Q(RegBEX), .clr(reset));
  Register register_4 (.D(R0ID), .en(we), .clk(clock_1_out), .Q(R0EX), .clr(reset));
  Register register_5 (.D(ImmID), .en(we), .clk(clock_1_out), .Q(immEX), .clr(reset));
  Register #(.width(3)) register_6 (.D(UlaCtrlID), .en(we), .clk(clock_1_out), .Q(UlaCtrlEX), .clr(reset));
  Register #(.width(2)) register_7 (.D(BranchTID), .en(we), .clk(clock_1_out), .Q(BranchTEX), .clr(reset));
  Register #(.width(1)) register_8 (.D(r0ctrlID), .en(we), .clk(clock_1_out), .Q(r0ctrlEX), .clr(reset));
  Register #(.width(1)) register_9 (.D(MemReadID), .en(we), .clk(clock_1_out), .Q(MemReadEX), .clr(reset));
  Register #(.width(1)) register_10 (.D(MemWriteID), .en(we), .clk(clock_1_out), .Q(MemWriteEX), .clr(reset));
  Register #(.width(2)) register_11 (.D(MuxWriteID), .en(we), .clk(clock_1_out), .Q(MuxWriteEX), .clr(reset));
  Register #(.width(1)) register_12 (.D(MuxUlaID), .en(we), .clk(clock_1_out), .Q(MuxUlaEX), .clr(reset));
  Register #(.width(1)) register_13 (.D(RegWriteID), .en(we), .clk(clock_1_out), .Q(RegWriteEX), .clr(reset));
endmodule
